# Fritzing sketch TIMER attiny13 (saved by Fritzing 0.9.3b)
circuit board: 4cm x 4cm
breadboards: 1

parts:
  U1 = ATTINY13 [package=dip]
  -_+ = female pin header, 2 pins [form="♀ (female)"]
  K1 = OMRON PCB Power Relay – G5LE [part_number="G5LE-1\n" package=THT]
  J1 = Screw terminal - 2 pins [package=THT]
  B_-_+ = female pin header, 2 pins [form="♀ (female)"]
  Y_+_- = female pin header, 2 pins [form="♀ (female)"]
  R1 = Resistor [tolerance=±5% resistance=220 package=THT]
  R2 = Resistor [tolerance=±5% resistance=220 package=THT]
  R3 = Resistor [tolerance=±5% resistance=10k package=THT]
  R4 = Resistor [tolerance=±5% resistance=10k package=THT]
  BB = female pin header, 2 pins [form="♀ (female)"]
  BY = female pin header, 2 pins [form="♀ (female)"]
  R5 = Resistor [tolerance=±5% resistance=220 package=THT]
  L_+_- = female pin header, 2 pins [form="♀ (female)"]
  RST = female pin header, 2 pins [form="♀ (female)"]
  R6 = Resistor [tolerance=±5% resistance=10k package=THT]

nets:
  N1: U1.PB5(NRES), -_+.pin2, BB.pin2, BY.pin1
  N2: U1.PB3(ADC3), B_-_+.pin2, R3.Pin_1, BB.pin1
  N3: U1.PB4(ADC2), Y_+_-.pin1, R4.Pin_1, BY.pin2
  N4: U1.GND, K1.COIL2, L_+_-.pin1
  N5: U1.PB0(MOSI), -_+.pin1, K1.COIL1, R1.Pin_0, R2.Pin_0, R3.Pin_0, R4.Pin_0, R5.Pin_0, R6.Pin_1
  N6: U1.VCC, RST.pin1
  N7: K1.C, J1.pin2
  N8: K1.B, J1.pin1
  N9: B_-_+.pin1, R1.Pin_1
  N10: Y_+_-.pin2, R2.Pin_1
  N11: R5.Pin_1, L_+_-.pin2
  N12: RST.pin2, R6.Pin_0
